# Fritzing sketch espinet (saved by Fritzing 1.0.1rc)

parts:
  Mod1 = Raspberry Pi 4B
  J2 = Basic Servo
  J1 = Basic Servo
  Part1 = BME280 Breakout
  IC1 = Rasberry Pi NIOR Camera [chip_label=IC package="DIP (Dual Inline) [THT]"]  # not connected

nets:
  3V3: Mod1.3V3, Part1.3.3V
  VCC: Mod1.5V, J2.vcc, J1.vcc
  N1: Mod1.GPIO2, Part1.SDI/SDA
  N2: Mod1.GPIO3, Part1.SCK/SCL
  GND: Mod1.GND, J2.gnd, J1.gnd, Part1.GND
  N3: Mod1.GPIO17, J1.pulse
  N4: Mod1.GPIO18, J2.pulse

notes:
  Powered via USBC
  Cam Panning Servo
  Cam Tilt Servo

custom parts:
  Rasberry Pi NIOR Camera: Camera
